# Fritzing sketch simon (saved by Fritzing 0.9.1b)
breadboards: 1

parts:
  Onderdeel1 = Arduino Uno (Rev3)
  LED1 = LED - 5mm [color="Blue (430nm)" package="5 mm [THT]"]
  LED2 = LED - 5mm [color="Yellow (595nm)" package="5 mm [THT]"]
  LED3 = LED - 5mm [color="Green (555nm)" package="5 mm [THT]"]
  LED4 = LED - 5mm [color="Red (635nm)" package="5 mm [THT]"]
  S1 = Pushbutton [package="[THT]"]
  S2 = Pushbutton [package="[THT]"]
  S3 = Pushbutton [package="[THT]"]
  S4 = Pushbutton [package="[THT]"]
  R5 = Resistor [tolerance=±5% resistance=220 package=THT]
  R4 = Resistor [tolerance=±5% resistance=330 package=THT]
  R3 = Resistor [tolerance=±5% resistance=330 package=THT]
  R2 = Resistor [tolerance=±5% resistance=330 package=THT]
  R1 = Resistor [tolerance=±2% resistance=330 package=THT]
  R6 = Resistor [tolerance=±5% resistance=220 package=THT]
  R7 = Resistor [tolerance=±5% resistance=220 package=THT]
  R8 = Resistor [tolerance=±5% resistance=220 package=THT]

nets:
  N1: Onderdeel1.D9_PWM, S4.Pin_1, S4.Pin_2, R5.Pin_0
  N2: Onderdeel1.D10_PWM/SS, S3.Pin_1, S3.Pin_2, R6.Pin_0
  N3: Onderdeel1.D11_PWM/MOSI, S2.Pin_1, S2.Pin_2, R7.Pin_0
  N4: Onderdeel1.D12/MISO, S1.Pin_1, S1.Pin_2, R8.Pin_0
  N5: Onderdeel1.GND, LED1.cathode, LED2.cathode, LED3.cathode, LED4.cathode, S1.Pin_3, S1.Pin_4, S2.Pin_3, S2.Pin_4, S3.Pin_3, S3.Pin_4, S4.Pin_3, S4.Pin_4
  N6: Onderdeel1.D2, R1.Pin_0
  N7: Onderdeel1.D3_PWM, R4.Pin_0
  N8: Onderdeel1.D4, R3.Pin_0
  N9: Onderdeel1.D5_PWM, R2.Pin_0
  N10: Onderdeel1.5V, R5.Pin_1, R6.Pin_1, R7.Pin_1, R8.Pin_1
  N11: LED1.anode, R2.Pin_1
  N12: LED2.anode, R3.Pin_1
  N13: LED3.anode, R4.Pin_1
  N14: LED4.anode, R1.Pin_1

// code stored in the sketch: simon.ino
#include <SimpleList.h>

// LED pins
const int led1 = 5;
const int led2 = 4;
const int led3 = 3;
const int led4 = 2;

// Button pins
const int btn1 = 12;
const int btn2 = 11;
const int btn3 = 10;
const int btn4 = 9;

// Button state
int btn1State = 0;
int btn2State = 0;
int btn3State = 0;
int btn4State = 0;

// Variable to store pattern of current game
SimpleList <int> currentSong;
// Variable to store the current level
int currentLevel = 0;


void setup() {
  // Set LED pins as output
  pinMode(led1, OUTPUT);
  pinMode(led2, OUTPUT);
  pinMode(led3, OUTPUT);
  pinMode(led4, OUTPUT);
  
  // Set button pins as input
  pinMode(btn1, INPUT);
  pinMode(btn2, INPUT);
  pinMode(btn3, INPUT);
  pinMode(btn4, INPUT);
  
  // Get new random seed through analog noise
  randomSeed(analogRead(0));
}
  
void loop() {
  // Variable to store correct presses every turn 
  int goodNotes = 0;
  // Variable to store if last press was correct
  boolean ok = false;
  
  // Level up at the begin of every turn
  levelUp();

  do {
    int input = readButtons();
    ok = checkNote(goodNotes, input);
    goodNotes++;
  } while(goodNotes < currentLevel && ok);
  
  if (!ok) {
    currentSong.clear();
    currentLevel = 0;
  }
  
  delay(1500);
}

void levelUp() {
  currentLevel++;
  int randNote = random(1,5);
  
  currentSong.push_back(randNote);

  playSong();
}

boolean checkNote(int pos, int value) {
  int i = 0;
  for (SimpleList<int>::iterator itr = currentSong.begin(); itr != currentSong.end(); ++itr) {
     if (i == pos) {
       if ((*itr) == value) {
         return true;
       }else{
         return false; 
       }
     }
     i++;
  }
}

void playSong() {
  for (SimpleList<int>::iterator itr = currentSong.begin(); itr != currentSong.end(); ++itr) { 
    switch (*itr){
    case 1:
      digitalWrite(led1, HIGH);
      delay(1000);
      digitalWrite(led1, LOW);
      break;
    case 2:
      digitalWrite(led2, HIGH);
      delay(1000);
      digitalWrite(led2, LOW);
      break;
    case 3:
      digitalWrite(led3, HIGH);
      delay(1000);
      digitalWrite(led3, LOW);
      break;
    case 4:
      digitalWrite(led4, HIGH);
      delay(1000);
      digitalWrite(led4, LOW);
      break;
    }
    delay(400);
  }
}

int readButtons(){
  int down;
  
  do {
    btn1State = digitalRead(btn1); 
    btn2State = digitalRead(btn2); 
    btn3State = digitalRead(btn3); 
    btn4State = digitalRead(btn4); 
  
    if (btn1State == LOW) {
      down = 1;
      digitalWrite(led1, HIGH);
      delay(500);
      digitalWrite(led1, LOW);
    } else if (btn2State == LOW) {
      down = 2;
      digitalWrite(led2, HIGH);
      delay(500);
      digitalWrite(led2, LOW);
    } else if (btn3State == LOW) {
      down = 3;
      digitalWrite(led3, HIGH);
      delay(500);
      digitalWrite(led3, LOW);
    } else if (btn4State == LOW) {
      down = 4;
      digitalWrite(led4, HIGH);
      delay(500);
      digitalWrite(led4, LOW);
    } else {
      down = 0;
    }  
  }while(down == 0);

  return down;
}
